// Logisim project CPU.circ as structural Verilog: 4 circuits, main circuit CPU32
// REGS
module REGS16_32 (
  input  [3:0] REG_A_ADDR,
  input  [3:0] REG_B_ADDR,
  input  [3:0] REG_C_ADDR,
  input  [3:0] REG_D_ADDR,
  input  _0_ENA,
  input  CLK,
  input  A_ENA,
  input  A_WE,
  input  [31:0] A_IN,
  input  B_ENA,
  input  B_WE,
  input  [31:0] B_IN,
  input  C_ENA,
  input  C_WE,
  input  [31:0] C_IN,
  input  D_ENA,
  input  D_WE,
  input  [31:0] D_IN,
  output [31:0] A_OUT,
  output [31:0] B_OUT,
  output [31:0] C_OUT,
  output [31:0] D_OUT
);

  wire A_0, A_1, A_2, A_3, A_4, A_5, A_6, A_7, A_8, A_9, A_A, A_B, A_C, A_D, A_E, A_F, and_2_out, and_3_out,
       and_4_out, and_5_out, and_6_out, and_7_out, and_8_out, and_9_out, and_10_out, and_11_out, and_12_out,
       and_13_out, and_14_out, and_15_out, and_16_out, and_17_out, and_18_out, and_19_out, and_20_out,
       and_21_out, and_22_out, and_23_out, and_24_out, and_25_out, and_26_out, and_27_out, and_28_out,
       and_29_out, and_30_out, and_31_out, and_32_out, and_33_out, and_34_out, and_35_out, and_36_out,
       and_37_out, and_38_out, and_39_out, and_40_out, and_41_out, and_42_out, and_43_out, and_44_out,
       and_45_out, and_46_out, and_47_out, and_48_out, and_49_out, and_50_out, and_51_out, and_52_out,
       and_53_out, and_54_out, and_55_out, and_56_out, and_57_out, and_58_out, and_59_out, and_60_out,
       and_61_out, and_62_out, and_63_out, and_64_out, and_65_out, B_0, B_1, B_2, B_3, B_4, B_5, B_6, B_7,
       B_8, B_9, B_A, B_B, B_C, B_D, B_E, B_F, C_0, C_1, C_2, C_3, C_4, C_5, C_6, C_7, C_8, C_9, C_A, C_B,
       C_C, C_D, C_E, C_F, D_0, D_1, D_2, D_3, D_4, D_5, D_6, D_7, D_8, D_9, D_A, D_B, D_C, D_D, D_E, D_F,
       or_1_out, or_2_out, or_3_out, or_4_out, or_5_out, or_6_out, or_7_out, or_8_out, or_9_out, or_10_out,
       or_11_out, or_12_out, or_13_out, or_14_out, or_15_out, or_16_out;
  wire [1:0] bitfinder_1_index, bitfinder_2_index, bitfinder_3_index, bitfinder_4_index, bitfinder_5_index,
       bitfinder_6_index, bitfinder_7_index, bitfinder_8_index, bitfinder_9_index, bitfinder_10_index,
       bitfinder_11_index, bitfinder_12_index, bitfinder_13_index, bitfinder_14_index, bitfinder_15_index,
       bitfinder_16_index;
  wire [3:0] and_1_out;
  wire [31:0] multiplexer_1_out, multiplexer_2_out, multiplexer_3_out, multiplexer_4_out, multiplexer_5_out,
       multiplexer_6_out, multiplexer_7_out, multiplexer_8_out, multiplexer_9_out, multiplexer_10_out,
       multiplexer_11_out, multiplexer_12_out, multiplexer_13_out, multiplexer_14_out, multiplexer_15_out,
       multiplexer_16_out, register_1_q, register_2_q, register_3_q, register_4_q, register_5_q,
       register_6_q, register_7_q, register_8_q, register_9_q, register_10_q, register_11_q, register_12_q,
       register_13_q, register_14_q, register_15_q, register_16_q;

  Decoder #(.select(4), .disabled(0)) decoder_1 (
    .out0(A_0), .out1(A_1), .out2(A_2), .out3(A_3), .out4(A_4), .out5(A_5), .out6(A_6), .out7(A_7),
    .out8(A_8), .out9(A_9), .out10(A_A), .out11(A_B), .out12(A_C), .out13(A_D), .out14(A_E), .out15(A_F),
    .sel(REG_A_ADDR), .en(A_ENA));
  Decoder #(.select(4), .disabled(0)) decoder_2 (
    .out0(B_0), .out1(B_1), .out2(B_2), .out3(B_3), .out4(B_4), .out5(B_5), .out6(B_6), .out7(B_7),
    .out8(B_8), .out9(B_9), .out10(B_A), .out11(B_B), .out12(B_C), .out13(B_D), .out14(B_E), .out15(B_F),
    .sel(REG_B_ADDR), .en(B_ENA));
  Decoder #(.select(4), .disabled(0)) decoder_3 (
    .out0(C_0), .out1(C_1), .out2(C_2), .out3(C_3), .out4(C_4), .out5(C_5), .out6(C_6), .out7(C_7),
    .out8(C_8), .out9(C_9), .out10(C_A), .out11(C_B), .out12(C_C), .out13(C_D), .out14(C_E), .out15(C_F),
    .sel(REG_C_ADDR), .en(C_ENA));
  Decoder #(.select(4), .disabled(0)) decoder_4 (
    .out0(D_0), .out1(D_1), .out2(D_2), .out3(D_3), .out4(D_4), .out5(D_5), .out6(D_6), .out7(D_7),
    .out8(D_8), .out9(D_9), .out10(D_A), .out11(D_B), .out12(D_C), .out13(D_D), .out14(D_E), .out15(D_F),
    .sel(REG_D_ADDR), .en(D_ENA));
  BitFinder #(.width(4), .\type ("high1")) bitfinder_1 (
    .in({D_0, C_0, B_0, A_0}), .index(bitfinder_1_index));  // open: found
  assign and_1_out = {D_1, C_1, B_1, A_1} & {D_WE, C_WE, B_WE, A_WE};  // AND_Gate and_1, 4 bits wide
  BitFinder #(.width(4), .\type ("high1")) bitfinder_2 (
    .in({D_4, C_4, B_4, A_4}), .index(bitfinder_2_index));  // open: found
  BitFinder #(.width(4), .\type ("high1")) bitfinder_3 (
    .in({D_5, C_5, B_5, A_5}), .index(bitfinder_3_index));  // open: found
  // Probe on bitfinder_1_index
  Multiplexer #(.select(2), .width(32), .disabled(0), .enable("false")) multiplexer_1 (
    .in0(A_IN), .in1(B_IN), .in2(C_IN), .in3(D_IN), .out(multiplexer_1_out), .sel(bitfinder_1_index));
  or or_1 (or_1_out, A_0, B_0, C_0, D_0);
  BitFinder #(.width(4), .\type ("high1")) bitfinder_4 (.in(and_1_out), .index(bitfinder_4_index));  // open: found
  // Probe on bitfinder_4_index
  Multiplexer #(.select(2), .width(32), .disabled(0), .enable("false")) multiplexer_2 (
    .in0(A_IN), .in1(B_IN), .in2(C_IN), .in3(D_IN), .out(multiplexer_2_out), .sel(bitfinder_4_index));
  or or_2 (or_2_out, A_1, B_1, C_1, D_1);
  // Probe on bitfinder_2_index
  Multiplexer #(.select(2), .width(32), .disabled(0), .enable("false")) multiplexer_3 (
    .in0(A_IN), .in1(B_IN), .in2(C_IN), .in3(D_IN), .out(multiplexer_3_out), .sel(bitfinder_2_index));
  or or_3 (or_3_out, A_4, B_4, C_4, D_4);
  // Probe on bitfinder_3_index
  Multiplexer #(.select(2), .width(32), .disabled(0), .enable("false")) multiplexer_4 (
    .in0(A_IN), .in1(B_IN), .in2(C_IN), .in3(D_IN), .out(multiplexer_4_out), .sel(bitfinder_3_index));
  or or_4 (or_4_out, A_5, B_5, C_5, D_5);
  and and_2 (and_2_out, A_0, ~A_WE);  // AND_Gate
  Register #(.width(32)) register_1 (.D(multiplexer_1_out), .en(or_1_out), .Q(register_1_q), .clk(CLK), .clr(_0_ENA));
  assign A_OUT = and_2_out ? register_1_q : 32'bz;  // Controlled_Buffer controlled_buffer_1
  and and_3 (and_3_out, A_1, ~A_WE);  // AND_Gate
  Register #(.width(32)) register_2 (.D(multiplexer_2_out), .en(or_2_out), .Q(register_2_q), .clk(CLK));  // open: clr
  assign A_OUT = and_3_out ? register_2_q : 32'bz;  // Controlled_Buffer controlled_buffer_2
  and and_4 (and_4_out, A_4, ~A_WE);  // AND_Gate
  Register #(.width(32)) register_3 (.D(multiplexer_3_out), .en(or_3_out), .Q(register_3_q), .clk(CLK));  // open: clr
  assign A_OUT = and_4_out ? register_3_q : 32'bz;  // Controlled_Buffer controlled_buffer_3
  and and_5 (and_5_out, A_5, ~A_WE);  // AND_Gate
  Register #(.width(32)) register_4 (.D(multiplexer_4_out), .en(or_4_out), .Q(register_4_q), .clk(CLK));  // open: clr
  assign A_OUT = and_5_out ? register_4_q : 32'bz;  // Controlled_Buffer controlled_buffer_4
  and and_6 (and_6_out, B_0, ~B_WE);  // AND_Gate
  and and_7 (and_7_out, C_0, ~C_WE);  // AND_Gate
  assign B_OUT = and_6_out ? register_1_q : 32'bz;  // Controlled_Buffer controlled_buffer_5
  assign C_OUT = and_7_out ? register_1_q : 32'bz;  // Controlled_Buffer controlled_buffer_6
  and and_8 (and_8_out, C_1, ~C_WE);  // AND_Gate
  and and_9 (and_9_out, B_1, ~B_WE);  // AND_Gate
  assign B_OUT = and_9_out ? register_2_q : 32'bz;  // Controlled_Buffer controlled_buffer_7
  assign C_OUT = and_8_out ? register_2_q : 32'bz;  // Controlled_Buffer controlled_buffer_8
  and and_10 (and_10_out, B_4, ~B_WE);  // AND_Gate
  and and_11 (and_11_out, C_4, ~C_WE);  // AND_Gate
  assign B_OUT = and_10_out ? register_3_q : 32'bz;  // Controlled_Buffer controlled_buffer_9
  assign C_OUT = and_11_out ? register_3_q : 32'bz;  // Controlled_Buffer controlled_buffer_10
  and and_12 (and_12_out, C_5, ~C_WE);  // AND_Gate
  and and_13 (and_13_out, B_5, ~B_WE);  // AND_Gate
  assign C_OUT = and_12_out ? register_4_q : 32'bz;  // Controlled_Buffer controlled_buffer_11
  assign B_OUT = and_13_out ? register_4_q : 32'bz;  // Controlled_Buffer controlled_buffer_12
  and and_14 (and_14_out, D_0, ~D_WE);  // AND_Gate
  assign D_OUT = and_14_out ? register_1_q : 32'bz;  // Controlled_Buffer controlled_buffer_13
  and and_15 (and_15_out, D_1, ~D_WE);  // AND_Gate
  assign D_OUT = and_15_out ? register_2_q : 32'bz;  // Controlled_Buffer controlled_buffer_14
  and and_16 (and_16_out, D_4, ~D_WE);  // AND_Gate
  assign D_OUT = and_16_out ? register_3_q : 32'bz;  // Controlled_Buffer controlled_buffer_15
  and and_17 (and_17_out, D_5, ~D_WE);  // AND_Gate
  assign D_OUT = and_17_out ? register_4_q : 32'bz;  // Controlled_Buffer controlled_buffer_16
  BitFinder #(.width(4), .\type ("high1")) bitfinder_5 (
    .in({D_2, C_2, B_2, A_2}), .index(bitfinder_5_index));  // open: found
  // Probe on bitfinder_5_index
  Multiplexer #(.select(2), .width(32), .disabled(0), .enable("false")) multiplexer_5 (
    .in0(A_IN), .in1(B_IN), .in2(C_IN), .in3(D_IN), .out(multiplexer_5_out), .sel(bitfinder_5_index));
  BitFinder #(.width(4), .\type ("high1")) bitfinder_6 (
    .in({D_3, C_3, B_3, A_3}), .index(bitfinder_6_index));  // open: found
  // Probe on bitfinder_6_index
  Multiplexer #(.select(2), .width(32), .disabled(0), .enable("false")) multiplexer_6 (
    .in0(A_IN), .in1(B_IN), .in2(C_IN), .in3(D_IN), .out(multiplexer_6_out), .sel(bitfinder_6_index));
  BitFinder #(.width(4), .\type ("high1")) bitfinder_7 (
    .in({D_6, C_6, B_6, A_6}), .index(bitfinder_7_index));  // open: found
  // Probe on bitfinder_7_index
  Multiplexer #(.select(2), .width(32), .disabled(0), .enable("false")) multiplexer_7 (
    .in0(A_IN), .in1(B_IN), .in2(C_IN), .in3(D_IN), .out(multiplexer_7_out), .sel(bitfinder_7_index));
  BitFinder #(.width(4), .\type ("high1")) bitfinder_8 (
    .in({D_7, C_7, B_7, A_7}), .index(bitfinder_8_index));  // open: found
  // Probe on bitfinder_8_index
  Multiplexer #(.select(2), .width(32), .disabled(0), .enable("false")) multiplexer_8 (
    .in0(A_IN), .in1(B_IN), .in2(C_IN), .in3(D_IN), .out(multiplexer_8_out), .sel(bitfinder_8_index));
  Register #(.width(32)) register_5 (.D(multiplexer_5_out), .en(or_5_out), .Q(register_5_q), .clk(CLK));  // open: clr
  or or_5 (or_5_out, A_2, B_2, C_2, D_2);
  Register #(.width(32)) register_6 (.D(multiplexer_6_out), .en(or_6_out), .Q(register_6_q), .clk(CLK));  // open: clr
  or or_6 (or_6_out, A_3, B_3, C_3, D_3);
  Register #(.width(32)) register_7 (.D(multiplexer_7_out), .en(or_7_out), .Q(register_7_q), .clk(CLK));  // open: clr
  or or_7 (or_7_out, A_6, B_6, C_6, D_6);
  Register #(.width(32)) register_8 (.D(multiplexer_8_out), .en(or_8_out), .Q(register_8_q), .clk(CLK));  // open: clr
  or or_8 (or_8_out, A_7, B_7, C_7, D_7);
  and and_18 (and_18_out, A_2, ~A_WE);  // AND_Gate
  and and_19 (and_19_out, B_2, ~B_WE);  // AND_Gate
  assign A_OUT = and_18_out ? register_5_q : 32'bz;  // Controlled_Buffer controlled_buffer_17
  assign B_OUT = and_19_out ? register_5_q : 32'bz;  // Controlled_Buffer controlled_buffer_18
  and and_20 (and_20_out, A_3, ~A_WE);  // AND_Gate
  and and_21 (and_21_out, B_3, ~B_WE);  // AND_Gate
  assign A_OUT = and_20_out ? register_6_q : 32'bz;  // Controlled_Buffer controlled_buffer_19
  assign B_OUT = and_21_out ? register_6_q : 32'bz;  // Controlled_Buffer controlled_buffer_20
  and and_22 (and_22_out, A_6, ~A_WE);  // AND_Gate
  and and_23 (and_23_out, B_6, ~B_WE);  // AND_Gate
  assign A_OUT = and_22_out ? register_7_q : 32'bz;  // Controlled_Buffer controlled_buffer_21
  assign B_OUT = and_23_out ? register_7_q : 32'bz;  // Controlled_Buffer controlled_buffer_22
  and and_24 (and_24_out, A_7, ~A_WE);  // AND_Gate
  and and_25 (and_25_out, B_7, ~B_WE);  // AND_Gate
  assign A_OUT = and_24_out ? register_8_q : 32'bz;  // Controlled_Buffer controlled_buffer_23
  assign B_OUT = and_25_out ? register_8_q : 32'bz;  // Controlled_Buffer controlled_buffer_24
  and and_26 (and_26_out, C_2, ~C_WE);  // AND_Gate
  assign D_OUT = and_30_out ? register_5_q : 32'bz;  // Controlled_Buffer controlled_buffer_25
  assign C_OUT = and_26_out ? register_5_q : 32'bz;  // Controlled_Buffer controlled_buffer_26
  and and_27 (and_27_out, C_3, ~C_WE);  // AND_Gate
  assign D_OUT = and_31_out ? register_6_q : 32'bz;  // Controlled_Buffer controlled_buffer_27
  assign C_OUT = and_27_out ? register_6_q : 32'bz;  // Controlled_Buffer controlled_buffer_28
  and and_28 (and_28_out, C_6, ~C_WE);  // AND_Gate
  assign D_OUT = and_32_out ? register_7_q : 32'bz;  // Controlled_Buffer controlled_buffer_29
  assign C_OUT = and_28_out ? register_7_q : 32'bz;  // Controlled_Buffer controlled_buffer_30
  and and_29 (and_29_out, C_7, ~C_WE);  // AND_Gate
  assign C_OUT = and_29_out ? register_8_q : 32'bz;  // Controlled_Buffer controlled_buffer_31
  assign D_OUT = and_33_out ? register_8_q : 32'bz;  // Controlled_Buffer controlled_buffer_32
  and and_30 (and_30_out, D_2, ~D_WE);  // AND_Gate
  and and_31 (and_31_out, D_3, ~D_WE);  // AND_Gate
  and and_32 (and_32_out, D_6, ~D_WE);  // AND_Gate
  and and_33 (and_33_out, D_7, ~D_WE);  // AND_Gate
  BitFinder #(.width(4), .\type ("high1")) bitfinder_9 (
    .in({D_8, C_8, B_8, A_8}), .index(bitfinder_9_index));  // open: found
  BitFinder #(.width(4), .\type ("high1")) bitfinder_10 (
    .in({D_9, C_9, B_9, A_9}), .index(bitfinder_10_index));  // open: found
  BitFinder #(.width(4), .\type ("high1")) bitfinder_11 (
    .in({D_A, C_A, B_A, A_A}), .index(bitfinder_11_index));  // open: found
  BitFinder #(.width(4), .\type ("high1")) bitfinder_12 (
    .in({D_B, C_B, B_B, A_B}), .index(bitfinder_12_index));  // open: found
  // Probe on bitfinder_9_index
  Multiplexer #(.select(2), .width(32), .disabled(0), .enable("false")) multiplexer_9 (
    .in0(A_IN), .in1(B_IN), .in2(C_IN), .in3(D_IN), .out(multiplexer_9_out), .sel(bitfinder_9_index));
  or or_9 (or_9_out, A_8, B_8, C_8, D_8);
  // Probe on bitfinder_10_index
  Multiplexer #(.select(2), .width(32), .disabled(0), .enable("false")) multiplexer_10 (
    .in0(A_IN), .in1(B_IN), .in2(C_IN), .in3(D_IN), .out(multiplexer_10_out), .sel(bitfinder_10_index));
  or or_10 (or_10_out, A_9, B_9, C_9, D_9);
  // Probe on bitfinder_11_index
  Multiplexer #(.select(2), .width(32), .disabled(0), .enable("false")) multiplexer_11 (
    .in0(A_IN), .in1(B_IN), .in2(C_IN), .in3(D_IN), .out(multiplexer_11_out), .sel(bitfinder_11_index));
  or or_11 (or_11_out, A_A, B_A, C_A, D_A);
  // Probe on bitfinder_12_index
  Multiplexer #(.select(2), .width(32), .disabled(0), .enable("false")) multiplexer_12 (
    .in0(A_IN), .in1(B_IN), .in2(C_IN), .in3(D_IN), .out(multiplexer_12_out), .sel(bitfinder_12_index));
  or or_12 (or_12_out, A_B, B_B, C_B, D_B);
  and and_34 (and_34_out, A_8, ~A_WE);  // AND_Gate
  Register #(.width(32)) register_9 (.D(multiplexer_9_out), .en(or_9_out), .Q(register_9_q), .clk(CLK));  // open: clr
  assign A_OUT = and_34_out ? register_9_q : 32'bz;  // Controlled_Buffer controlled_buffer_33
  and and_35 (and_35_out, A_9, ~A_WE);  // AND_Gate
  Register #(.width(32)) register_10 (
    .D(multiplexer_10_out), .en(or_10_out), .Q(register_10_q), .clk(CLK));  // open: clr
  assign A_OUT = and_35_out ? register_10_q : 32'bz;  // Controlled_Buffer controlled_buffer_34
  and and_36 (and_36_out, A_A, ~A_WE);  // AND_Gate
  Register #(.width(32)) register_11 (
    .D(multiplexer_11_out), .en(or_11_out), .Q(register_11_q), .clk(CLK));  // open: clr
  assign A_OUT = and_36_out ? register_11_q : 32'bz;  // Controlled_Buffer controlled_buffer_35
  and and_37 (and_37_out, A_B, ~A_WE);  // AND_Gate
  Register #(.width(32)) register_12 (
    .D(multiplexer_12_out), .en(or_12_out), .Q(register_12_q), .clk(CLK));  // open: clr
  assign A_OUT = and_37_out ? register_12_q : 32'bz;  // Controlled_Buffer controlled_buffer_36
  and and_38 (and_38_out, B_8, ~B_WE);  // AND_Gate
  and and_39 (and_39_out, C_8, ~C_WE);  // AND_Gate
  assign C_OUT = and_39_out ? register_9_q : 32'bz;  // Controlled_Buffer controlled_buffer_37
  assign B_OUT = and_38_out ? register_9_q : 32'bz;  // Controlled_Buffer controlled_buffer_38
  and and_40 (and_40_out, C_9, ~C_WE);  // AND_Gate
  and and_41 (and_41_out, B_9, ~B_WE);  // AND_Gate
  assign B_OUT = and_41_out ? register_10_q : 32'bz;  // Controlled_Buffer controlled_buffer_39
  assign C_OUT = and_40_out ? register_10_q : 32'bz;  // Controlled_Buffer controlled_buffer_40
  and and_42 (and_42_out, C_A, ~C_WE);  // AND_Gate
  and and_43 (and_43_out, B_A, ~B_WE);  // AND_Gate
  assign C_OUT = and_42_out ? register_11_q : 32'bz;  // Controlled_Buffer controlled_buffer_41
  assign B_OUT = and_43_out ? register_11_q : 32'bz;  // Controlled_Buffer controlled_buffer_42
  and and_44 (and_44_out, C_B, ~C_WE);  // AND_Gate
  and and_45 (and_45_out, B_B, ~B_WE);  // AND_Gate
  assign B_OUT = and_45_out ? register_12_q : 32'bz;  // Controlled_Buffer controlled_buffer_43
  assign C_OUT = and_44_out ? register_12_q : 32'bz;  // Controlled_Buffer controlled_buffer_44
  and and_46 (and_46_out, D_8, ~D_WE);  // AND_Gate
  assign D_OUT = and_46_out ? register_9_q : 32'bz;  // Controlled_Buffer controlled_buffer_45
  and and_47 (and_47_out, D_9, ~D_WE);  // AND_Gate
  assign D_OUT = and_47_out ? register_10_q : 32'bz;  // Controlled_Buffer controlled_buffer_46
  and and_48 (and_48_out, D_A, ~D_WE);  // AND_Gate
  assign D_OUT = and_48_out ? register_11_q : 32'bz;  // Controlled_Buffer controlled_buffer_47
  and and_49 (and_49_out, D_B, ~D_WE);  // AND_Gate
  assign D_OUT = and_49_out ? register_12_q : 32'bz;  // Controlled_Buffer controlled_buffer_48
  BitFinder #(.width(4), .\type ("high1")) bitfinder_13 (
    .in({D_C, C_C, B_C, A_C}), .index(bitfinder_13_index));  // open: found
  // Probe on bitfinder_13_index
  Multiplexer #(.select(2), .width(32), .disabled(0), .enable("false")) multiplexer_13 (
    .in0(A_IN), .in1(B_IN), .in2(C_IN), .in3(D_IN), .out(multiplexer_13_out), .sel(bitfinder_13_index));
  BitFinder #(.width(4), .\type ("high1")) bitfinder_14 (
    .in({D_D, C_D, B_D, A_D}), .index(bitfinder_14_index));  // open: found
  // Probe on bitfinder_14_index
  Multiplexer #(.select(2), .width(32), .disabled(0), .enable("false")) multiplexer_14 (
    .in0(A_IN), .in1(B_IN), .in2(C_IN), .in3(D_IN), .out(multiplexer_14_out), .sel(bitfinder_14_index));
  BitFinder #(.width(4), .\type ("high1")) bitfinder_15 (
    .in({D_E, C_E, B_E, A_E}), .index(bitfinder_15_index));  // open: found
  // Probe on bitfinder_15_index
  Multiplexer #(.select(2), .width(32), .disabled(0), .enable("false")) multiplexer_15 (
    .in0(A_IN), .in1(B_IN), .in2(C_IN), .in3(D_IN), .out(multiplexer_15_out), .sel(bitfinder_15_index));
  BitFinder #(.width(4), .\type ("high1")) bitfinder_16 (
    .in({D_F, C_F, B_F, A_F}), .index(bitfinder_16_index));  // open: found
  // Probe on bitfinder_16_index
  Multiplexer #(.select(2), .width(32), .disabled(0), .enable("false")) multiplexer_16 (
    .in0(A_IN), .in1(B_IN), .in2(C_IN), .in3(D_IN), .out(multiplexer_16_out), .sel(bitfinder_16_index));
  Register #(.width(32)) register_13 (
    .D(multiplexer_13_out), .en(or_13_out), .Q(register_13_q), .clk(CLK));  // open: clr
  or or_13 (or_13_out, A_C, B_C, C_C, D_C);
  Register #(.width(32)) register_14 (
    .D(multiplexer_14_out), .en(or_14_out), .Q(register_14_q), .clk(CLK));  // open: clr
  or or_14 (or_14_out, A_D, B_D, C_D, D_D);
  Register #(.width(32)) register_15 (
    .D(multiplexer_15_out), .en(or_15_out), .Q(register_15_q), .clk(CLK));  // open: clr
  or or_15 (or_15_out, A_E, B_E, C_E, D_E);
  Register #(.width(32)) register_16 (
    .D(multiplexer_16_out), .en(or_16_out), .Q(register_16_q), .clk(CLK));  // open: clr
  or or_16 (or_16_out, A_F, B_F, C_F, D_F);
  and and_50 (and_50_out, A_C, ~A_WE);  // AND_Gate
  and and_51 (and_51_out, B_C, ~B_WE);  // AND_Gate
  assign A_OUT = and_50_out ? register_13_q : 32'bz;  // Controlled_Buffer controlled_buffer_49
  assign B_OUT = and_51_out ? register_13_q : 32'bz;  // Controlled_Buffer controlled_buffer_50
  and and_52 (and_52_out, B_D, ~B_WE);  // AND_Gate
  and and_53 (and_53_out, A_D, ~A_WE);  // AND_Gate
  assign A_OUT = and_53_out ? register_14_q : 32'bz;  // Controlled_Buffer controlled_buffer_51
  assign B_OUT = and_52_out ? register_14_q : 32'bz;  // Controlled_Buffer controlled_buffer_52
  and and_54 (and_54_out, A_E, ~A_WE);  // AND_Gate
  and and_55 (and_55_out, B_E, ~B_WE);  // AND_Gate
  assign B_OUT = and_55_out ? register_15_q : 32'bz;  // Controlled_Buffer controlled_buffer_53
  assign A_OUT = and_54_out ? register_15_q : 32'bz;  // Controlled_Buffer controlled_buffer_54
  and and_56 (and_56_out, B_F, ~B_WE);  // AND_Gate
  and and_57 (and_57_out, A_F, ~A_WE);  // AND_Gate
  assign B_OUT = and_56_out ? register_16_q : 32'bz;  // Controlled_Buffer controlled_buffer_55
  assign A_OUT = and_57_out ? register_16_q : 32'bz;  // Controlled_Buffer controlled_buffer_56
  and and_58 (and_58_out, C_C, ~C_WE);  // AND_Gate
  assign C_OUT = and_58_out ? register_13_q : 32'bz;  // Controlled_Buffer controlled_buffer_57
  assign D_OUT = and_62_out ? register_13_q : 32'bz;  // Controlled_Buffer controlled_buffer_58
  and and_59 (and_59_out, C_D, ~C_WE);  // AND_Gate
  assign D_OUT = and_63_out ? register_14_q : 32'bz;  // Controlled_Buffer controlled_buffer_59
  assign C_OUT = and_59_out ? register_14_q : 32'bz;  // Controlled_Buffer controlled_buffer_60
  and and_60 (and_60_out, C_E, ~C_WE);  // AND_Gate
  assign D_OUT = and_64_out ? register_15_q : 32'bz;  // Controlled_Buffer controlled_buffer_61
  assign C_OUT = and_60_out ? register_15_q : 32'bz;  // Controlled_Buffer controlled_buffer_62
  and and_61 (and_61_out, C_F, ~C_WE);  // AND_Gate
  assign D_OUT = and_65_out ? register_16_q : 32'bz;  // Controlled_Buffer controlled_buffer_63
  assign C_OUT = and_61_out ? register_16_q : 32'bz;  // Controlled_Buffer controlled_buffer_64
  and and_62 (and_62_out, D_C, ~D_WE);  // AND_Gate
  and and_63 (and_63_out, D_D, ~D_WE);  // AND_Gate
  and and_64 (and_64_out, D_E, ~D_WE);  // AND_Gate
  and and_65 (and_65_out, D_F, ~D_WE);  // AND_Gate

  // Notes on the sheet:
  //   A_WE: pull=down
  //   A_OUT: pull=down
  //   B_ENA: pull=down
  //   CLK: pull=down
  //   C_WE: pull=down
  //   REG_B_ADDR: pull=down
  //   A_ENA: pull=down
  //   _0_ENA: pull=down
  //   D_OUT: pull=down
  //   B_OUT: pull=down
  //   D_WE: pull=down
  //   C_OUT: pull=down
  //   REG_C_ADDR: pull=down
  //   B_WE: pull=down
  //   C_ENA: pull=down
  //   REG_D_ADDR: pull=down
  //   REG_A_ADDR: pull=down
  //   D_ENA: pull=down
endmodule

module CPU32 (
  input  [31:0] INSTRUCTION
);

  wire REG_A_ENA, REG_A_WE, REG_B_ENA, REG_B_WE, REG_C_ENA, REG_C_WE, REG_D_ENA, REG_D_WE, RI, RII, RRII,
       RRIL, RRIS, RRR, RRRR, RRRRI;
  wire [3:0] controlled_buffer_11_out, controlled_buffer_12_out, controlled_buffer_13_out,
       controlled_buffer_14_out, controlled_buffer_19_out, controlled_buffer_20_out,
       controlled_buffer_25_out, controlled_buffer_26_out;
  wire [5:0] controlled_buffer_4_out, controlled_buffer_5_out, controlled_buffer_6_out,
       controlled_buffer_7_out;
  wire [7:0] IMM8_0, IMM8_1, REG_A_ADDR, REG_B_ADDR, REG_C_ADDR, REG_D_ADDR, undriven, undriven_2;
  wire [15:0] IMM16;
  wire [31:0] REG_A_DATA, REG_B_DATA, REG_C_DATA, REG_D_DATA;

  Decoder #(.select(3), .enable("false")) decoder_1 (
    .out0(RRR), .out1(RRIL), .out2(RII), .out3(RI), .out4(RRRR), .out5(RRRRI), .out6(RRII), .out7(RRIS),
    .sel(INSTRUCTION[2:0]));
  assign REG_A_ADDR = RRR ? INSTRUCTION[15:8] : 8'bz;  // Controlled_Buffer controlled_buffer_1
  assign REG_B_ADDR = RRR ? INSTRUCTION[23:16] : 8'bz;  // Controlled_Buffer controlled_buffer_2
  assign REG_C_ADDR = RRR ? INSTRUCTION[31:24] : 8'bz;  // Controlled_Buffer controlled_buffer_3
  assign controlled_buffer_4_out = RRRR ? INSTRUCTION[13:8] : 6'bz;  // Controlled_Buffer controlled_buffer_4
  assign controlled_buffer_5_out = RRRR ? INSTRUCTION[19:14] : 6'bz;  // Controlled_Buffer controlled_buffer_5
  assign controlled_buffer_6_out = RRRR ? INSTRUCTION[25:20] : 6'bz;  // Controlled_Buffer controlled_buffer_6
  assign controlled_buffer_7_out = RRRR ? INSTRUCTION[31:26] : 6'bz;  // Controlled_Buffer controlled_buffer_7
  assign REG_A_ADDR = {{2{1'b0}}, controlled_buffer_4_out};  // Bit_Extender bit_extender_1
  assign REG_B_ADDR = {{2{1'b0}}, controlled_buffer_5_out};  // Bit_Extender bit_extender_2
  assign REG_C_ADDR = {{2{1'b0}}, controlled_buffer_6_out};  // Bit_Extender bit_extender_3
  assign REG_D_ADDR = {{2{1'b0}}, controlled_buffer_7_out};  // Bit_Extender bit_extender_4
  Pull_Resistor pull_resistor_1 (.node(REG_A_ADDR));
  Pull_Resistor pull_resistor_2 (.node(REG_B_ADDR));
  Pull_Resistor pull_resistor_3 (.node(REG_C_ADDR));
  Pull_Resistor pull_resistor_4 (.node(REG_D_ADDR));
  assign REG_A_ADDR = RRIL ? INSTRUCTION[15:8] : 8'bz;  // Controlled_Buffer controlled_buffer_8
  assign REG_B_ADDR = RRIL ? INSTRUCTION[23:16] : 8'bz;  // Controlled_Buffer controlled_buffer_9
  assign IMM8_0 = RRIL ? INSTRUCTION[31:24] : 8'bz;  // Controlled_Buffer controlled_buffer_10
  assign REG_A_ADDR = {{4{1'b0}}, controlled_buffer_11_out};  // Bit_Extender bit_extender_5
  assign controlled_buffer_11_out = RRRRI ? INSTRUCTION[11:8] : 4'bz;  // Controlled_Buffer controlled_buffer_11
  assign REG_B_ADDR = {{4{1'b0}}, controlled_buffer_12_out};  // Bit_Extender bit_extender_6
  assign controlled_buffer_12_out = RRRRI ? INSTRUCTION[15:12] : 4'bz;  // Controlled_Buffer controlled_buffer_12
  assign controlled_buffer_13_out = RRRRI ? INSTRUCTION[19:16] : 4'bz;  // Controlled_Buffer controlled_buffer_13
  assign REG_C_ADDR = {{4{1'b0}}, controlled_buffer_13_out};  // Bit_Extender bit_extender_7
  assign controlled_buffer_14_out = RRRRI ? INSTRUCTION[23:20] : 4'bz;  // Controlled_Buffer controlled_buffer_14
  assign REG_D_ADDR = {{4{1'b0}}, controlled_buffer_14_out};  // Bit_Extender bit_extender_8
  assign IMM8_0 = RRRRI ? INSTRUCTION[31:24] : 8'bz;  // Controlled_Buffer controlled_buffer_15
  Pull_Resistor pull_resistor_5 (.node(REG_A_DATA));
  Pull_Resistor pull_resistor_6 (.node(REG_B_DATA));
  Pull_Resistor pull_resistor_7 (.node(REG_C_DATA));
  Pull_Resistor pull_resistor_8 (.node(REG_D_DATA));
  REGS256_32 regs256_32_1 (
    .A_ADDR(REG_A_ADDR), .A_IN(REG_A_DATA), .A_OUT(REG_A_DATA), .B_ADDR(undriven), .B_IN(REG_B_DATA),
    .B_OUT(REG_B_DATA), .C_ADDR(REG_C_ADDR), .C_IN(REG_C_DATA), .C_OUT(REG_C_DATA), .D_ADDR(undriven_2),
    .D_IN(REG_D_DATA), .D_OUT(REG_D_DATA), .A_ENA(REG_A_ENA), .A_WE(REG_A_WE), .B_ENA(REG_B_ENA),
    .B_WE(REG_B_WE), .C_ENA(REG_C_ENA), .C_WE(REG_C_WE), .D_ENA(REG_D_ENA), .D_WE(REG_D_WE));
  Pull_Resistor pull_resistor_9 (.node(REG_A_ENA));
  Pull_Resistor pull_resistor_10 (.node(REG_B_ENA));
  Pull_Resistor pull_resistor_11 (.node(REG_C_ENA));
  Pull_Resistor pull_resistor_12 (.node(REG_D_ENA));
  assign REG_A_ADDR = RII ? INSTRUCTION[15:8] : 8'bz;  // Controlled_Buffer controlled_buffer_16
  assign IMM8_0 = RII ? INSTRUCTION[23:16] : 8'bz;  // Controlled_Buffer controlled_buffer_17
  assign IMM8_1 = RII ? INSTRUCTION[31:24] : 8'bz;  // Controlled_Buffer controlled_buffer_18
  assign controlled_buffer_19_out = RRII ? INSTRUCTION[11:8] : 4'bz;  // Controlled_Buffer controlled_buffer_19
  assign controlled_buffer_20_out = RRII ? INSTRUCTION[15:12] : 4'bz;  // Controlled_Buffer controlled_buffer_20
  assign IMM8_0 = RRII ? INSTRUCTION[23:16] : 8'bz;  // Controlled_Buffer controlled_buffer_21
  assign IMM8_1 = RRII ? INSTRUCTION[31:24] : 8'bz;  // Controlled_Buffer controlled_buffer_22
  Pull_Resistor pull_resistor_13 (.node(REG_A_WE));
  Pull_Resistor pull_resistor_14 (.node(REG_C_WE));
  assign REG_A_ADDR = {{4{1'b0}}, controlled_buffer_19_out};  // Bit_Extender bit_extender_9
  assign REG_B_ADDR = {{4{1'b0}}, controlled_buffer_20_out};  // Bit_Extender bit_extender_10
  Pull_Resistor pull_resistor_15 (.node(REG_B_WE));
  Pull_Resistor pull_resistor_16 (.node(REG_D_WE));
  assign REG_A_ADDR = RI ? INSTRUCTION[15:8] : 8'bz;  // Controlled_Buffer controlled_buffer_23
  assign IMM16 = RI ? INSTRUCTION[31:16] : 16'bz;  // Controlled_Buffer controlled_buffer_24
  assign controlled_buffer_25_out = RRIS ? INSTRUCTION[11:8] : 4'bz;  // Controlled_Buffer controlled_buffer_25
  assign controlled_buffer_26_out = RRIS ? INSTRUCTION[15:12] : 4'bz;  // Controlled_Buffer controlled_buffer_26
  assign IMM16 = RRIS ? INSTRUCTION[31:16] : 16'bz;  // Controlled_Buffer controlled_buffer_27
  assign REG_A_ADDR = {{4{1'b0}}, controlled_buffer_25_out};  // Bit_Extender bit_extender_11
  assign REG_B_ADDR = {{4{1'b0}}, controlled_buffer_26_out};  // Bit_Extender bit_extender_12

  // Other names for the same wires on the sheet: BLK_A_6[5:0] = INSTRUCTION[13:8]; BLK_B[7:0] = INSTRUCTION[15:8];
  //   BLK_B_0[3:0] = INSTRUCTION[11:8]; BLK_B_1[3:0] = INSTRUCTION[15:12]; BLK_B_6[5:0] = INSTRUCTION[19:14];
  //   BLK_C[7:0] = INSTRUCTION[23:16]; BLK_C_0[3:0] = INSTRUCTION[19:16]; BLK_C_1[3:0] = INSTRUCTION[23:20];
  //   BLK_C_6[5:0] = INSTRUCTION[25:20]; BLK_D[7:0] = INSTRUCTION[31:24]; BLK_D_0[3:0] = INSTRUCTION[27:24];
  //   BLK_D_6[5:0] = INSTRUCTION[31:26]; BLK_D_1[3:0] = INSTRUCTION[31:28]; TYPE[2:0] = INSTRUCTION[2:0];
  //   OPCODE[4:0] = INSTRUCTION[7:3]

  // Notes on the sheet:
  //   INSTRUCTION: pull=down
endmodule

module REGS256_32 (
  input  A_ENA,
  input  A_WE,
  input  B_ENA,
  input  B_WE,
  input  C_ENA,
  input  C_WE,
  input  D_ENA,
  input  D_WE,
  input  [7:0] A_ADDR,
  input  [31:0] A_IN,
  input  [7:0] B_ADDR,
  input  [31:0] B_IN,
  input  [7:0] C_ADDR,
  input  [31:0] C_IN,
  input  [7:0] D_ADDR,
  input  [31:0] D_IN,
  output [31:0] A_OUT,
  output [31:0] B_OUT,
  output [31:0] C_OUT,
  output [31:0] D_OUT
);

  wire A_0, A_1, A_2, A_3, A_4, A_5, A_6, A_7, A_8, A_9, A_A, A_B, A_C, A_D, A_E, A_F, and_1_out, and_3_out,
       and_5_out, and_7_out, B_0, B_1, B_2, B_3, B_4, B_5, B_6, B_7, B_8, B_9, B_A, B_B, B_C, B_D, B_E, B_F,
       C_0, C_1, C_2, C_3, C_4, C_5, C_6, C_7, C_8, C_9, C_A, C_B, C_C, C_D, C_E, C_F, CLK, D_0, D_1, D_2,
       D_3, D_4, D_5, D_6, D_7, D_8, D_9, D_A, D_B, D_C, D_D, D_E, D_F, transmission_1_p2, transmission_2_p2,
       transmission_3_p2, transmission_4_p2;
  wire [31:0] A_DATA, B_DATA, C_DATA, D_DATA;

  Clock clock_1 (.out(CLK));
  // Transmission_Gate #(.width(32)) transmission_1: pin names not known; wires that end beside it: A_OUT, transmission_1_p2, A_DATA
  // Transmission_Gate #(.width(32)) transmission_2: pin names not known; wires that end beside it: B_OUT, transmission_2_p2, B_DATA
  // Transmission_Gate #(.width(32)) transmission_3: pin names not known; wires that end beside it: C_OUT, transmission_3_p2, C_DATA
  // Transmission_Gate #(.width(32)) transmission_4: pin names not known; wires that end beside it: D_OUT, transmission_4_p2, D_DATA
  and and_1 (and_1_out, A_ENA, A_WE);
  // NOT_Gate not_1 has open pins: in=and_1_out, out=open
  // Transmission_Gate #(.width(32)) transmission_5: pin names not known; wires that end beside it: A_IN, and_1_out, A_DATA
  and and_2 (transmission_1_p2, A_ENA, ~A_WE);  // AND_Gate
  // NOT_Gate not_2 has open pins: in=transmission_1_p2, out=open
  and and_3 (and_3_out, B_ENA, B_WE);
  // NOT_Gate not_3 has open pins: in=and_3_out, out=open
  // Transmission_Gate #(.width(32)) transmission_6: pin names not known; wires that end beside it: B_IN, and_3_out, B_DATA
  and and_4 (transmission_2_p2, B_ENA, ~B_WE);  // AND_Gate
  // NOT_Gate not_4 has open pins: in=transmission_2_p2, out=open
  and and_5 (and_5_out, C_ENA, C_WE);
  // NOT_Gate not_5 has open pins: in=and_5_out, out=open
  // Transmission_Gate #(.width(32)) transmission_7: pin names not known; wires that end beside it: C_IN, and_5_out, C_DATA
  and and_6 (transmission_3_p2, C_ENA, ~C_WE);  // AND_Gate
  // NOT_Gate not_6 has open pins: in=transmission_3_p2, out=open
  and and_7 (and_7_out, D_ENA, D_WE);
  // NOT_Gate not_7 has open pins: in=and_7_out, out=open
  // Transmission_Gate #(.width(32)) transmission_8: pin names not known; wires that end beside it: D_IN, and_7_out, D_DATA
  and and_8 (transmission_4_p2, D_ENA, ~D_WE);  // AND_Gate
  // NOT_Gate not_8 has open pins: in=transmission_4_p2, out=open
  Decoder #(.select(4), .disabled(0)) decoder_1 (
    .out0(A_0), .out1(A_1), .out2(A_2), .out3(A_3), .out4(A_4), .out5(A_5), .out6(A_6), .out7(A_7),
    .out8(A_8), .out9(A_9), .out10(A_A), .out11(A_B), .out12(A_C), .out13(A_D), .out14(A_E), .out15(A_F),
    .sel(A_ADDR[7:4]), .en(A_ENA));
  Decoder #(.select(4), .disabled(0)) decoder_2 (
    .out0(B_0), .out1(B_1), .out2(B_2), .out3(B_3), .out4(B_4), .out5(B_5), .out6(B_6), .out7(B_7),
    .out8(B_8), .out9(B_9), .out10(B_A), .out11(B_B), .out12(B_C), .out13(B_D), .out14(B_E), .out15(B_F),
    .sel(B_ADDR[7:4]), .en(B_ENA));
  Decoder #(.select(4), .disabled(0)) decoder_3 (
    .out0(C_0), .out1(C_1), .out2(C_2), .out3(C_3), .out4(C_4), .out5(C_5), .out6(C_6), .out7(C_7),
    .out8(C_8), .out9(C_9), .out10(C_A), .out11(C_B), .out12(C_C), .out13(C_D), .out14(C_E), .out15(C_F),
    .sel(C_ADDR[7:4]), .en(C_ENA));
  Decoder #(.select(4), .disabled(0)) decoder_4 (
    .out0(D_0), .out1(D_1), .out2(D_2), .out3(D_3), .out4(D_4), .out5(D_5), .out6(D_6), .out7(D_7),
    .out8(D_8), .out9(D_9), .out10(D_A), .out11(D_B), .out12(D_C), .out13(D_D), .out14(D_E), .out15(D_F),
    .sel(D_ADDR[7:4]), .en(D_ENA));
  REGS16_32 REG0 (
    .A_ENA(A_0), .A_WE(A_WE), .A_IN(A_DATA), .A_OUT(A_DATA), .B_ENA(B_0), .B_WE(B_WE), .B_IN(B_DATA),
    .B_OUT(B_DATA), .C_ENA(C_0), .C_WE(C_WE), .C_IN(C_DATA), .C_OUT(C_DATA), .REG_A_ADDR(A_ADDR[3:0]),
    .REG_B_ADDR(B_ADDR[3:0]), .REG_C_ADDR(C_ADDR[3:0]), .CLK(CLK), .REG_D_ADDR(D_ADDR[3:0]), .D_ENA(D_0),
    .D_WE(D_WE), .D_IN(D_DATA), .D_OUT(D_DATA), ._0_ENA(1'b1));
  REGS16_32 REG0_2 (
    .A_ENA(A_1), .A_WE(A_WE), .A_IN(A_DATA), .A_OUT(A_DATA), .B_ENA(B_1), .B_WE(B_WE), .B_IN(B_DATA),
    .B_OUT(B_DATA), .C_ENA(C_1), .C_WE(C_WE), .C_IN(C_DATA), .C_OUT(C_DATA), .REG_A_ADDR(A_ADDR[3:0]),
    .REG_B_ADDR(B_ADDR[3:0]), .REG_C_ADDR(C_ADDR[3:0]), .CLK(CLK), .REG_D_ADDR(D_ADDR[3:0]), .D_ENA(D_1),
    .D_WE(D_WE), .D_IN(D_DATA), .D_OUT(D_DATA));  // open: _0_ENA
  REGS16_32 REG0_3 (
    .A_ENA(A_2), .A_WE(A_WE), .A_IN(A_DATA), .A_OUT(A_DATA), .B_ENA(B_2), .B_WE(B_WE), .B_IN(B_DATA),
    .B_OUT(B_DATA), .C_ENA(C_2), .C_WE(C_WE), .C_IN(C_DATA), .C_OUT(C_DATA), .REG_A_ADDR(A_ADDR[3:0]),
    .REG_B_ADDR(B_ADDR[3:0]), .REG_C_ADDR(C_ADDR[3:0]), .CLK(CLK), .REG_D_ADDR(D_ADDR[3:0]), .D_ENA(D_2),
    .D_WE(D_WE), .D_IN(D_DATA), .D_OUT(D_DATA));  // open: _0_ENA
  REGS16_32 REG0_4 (
    .A_ENA(A_3), .A_WE(A_WE), .A_IN(A_DATA), .A_OUT(A_DATA), .B_ENA(B_3), .B_WE(B_WE), .B_IN(B_DATA),
    .B_OUT(B_DATA), .C_ENA(C_3), .C_WE(C_WE), .C_IN(C_DATA), .C_OUT(C_DATA), .REG_A_ADDR(A_ADDR[3:0]),
    .REG_B_ADDR(B_ADDR[3:0]), .REG_C_ADDR(C_ADDR[3:0]), .CLK(CLK), .REG_D_ADDR(D_ADDR[3:0]), .D_ENA(D_3),
    .D_WE(D_WE), .D_IN(D_DATA), .D_OUT(D_DATA));  // open: _0_ENA
  REGS16_32 REG0_5 (
    .A_ENA(A_4), .A_WE(A_WE), .A_IN(A_DATA), .A_OUT(A_DATA), .B_ENA(B_4), .B_WE(B_WE), .B_IN(B_DATA),
    .B_OUT(B_DATA), .C_ENA(C_4), .C_WE(C_WE), .C_IN(C_DATA), .C_OUT(C_DATA), .REG_A_ADDR(A_ADDR[3:0]),
    .REG_B_ADDR(B_ADDR[3:0]), .REG_C_ADDR(C_ADDR[3:0]), .CLK(CLK), .REG_D_ADDR(D_ADDR[3:0]), .D_ENA(D_4),
    .D_WE(D_WE), .D_IN(D_DATA), .D_OUT(D_DATA));  // open: _0_ENA
  REGS16_32 REG0_6 (
    .A_ENA(A_5), .A_WE(A_WE), .A_IN(A_DATA), .A_OUT(A_DATA), .B_ENA(B_5), .B_WE(B_WE), .B_IN(B_DATA),
    .B_OUT(B_DATA), .C_ENA(C_5), .C_WE(C_WE), .C_IN(C_DATA), .C_OUT(C_DATA), .REG_A_ADDR(A_ADDR[3:0]),
    .REG_B_ADDR(B_ADDR[3:0]), .REG_C_ADDR(C_ADDR[3:0]), .CLK(CLK), .REG_D_ADDR(D_ADDR[3:0]), .D_ENA(D_5),
    .D_WE(D_WE), .D_IN(D_DATA), .D_OUT(D_DATA));  // open: _0_ENA
  REGS16_32 REG0_7 (
    .A_ENA(A_6), .A_WE(A_WE), .A_IN(A_DATA), .A_OUT(A_DATA), .B_ENA(B_6), .B_WE(B_WE), .B_IN(B_DATA),
    .B_OUT(B_DATA), .C_ENA(C_6), .C_WE(C_WE), .C_IN(C_DATA), .C_OUT(C_DATA), .REG_A_ADDR(A_ADDR[3:0]),
    .REG_B_ADDR(B_ADDR[3:0]), .REG_C_ADDR(C_ADDR[3:0]), .CLK(CLK), .REG_D_ADDR(D_ADDR[3:0]), .D_ENA(D_6),
    .D_WE(D_WE), .D_IN(D_DATA), .D_OUT(D_DATA));  // open: _0_ENA
  REGS16_32 REG0_8 (
    .A_ENA(A_7), .A_WE(A_WE), .A_IN(A_DATA), .A_OUT(A_DATA), .B_ENA(B_7), .B_WE(B_WE), .B_IN(B_DATA),
    .B_OUT(B_DATA), .C_ENA(C_7), .C_WE(C_WE), .C_IN(C_DATA), .C_OUT(C_DATA), .REG_A_ADDR(A_ADDR[3:0]),
    .REG_B_ADDR(B_ADDR[3:0]), .REG_C_ADDR(C_ADDR[3:0]), .CLK(CLK), .REG_D_ADDR(D_ADDR[3:0]), .D_ENA(D_7),
    .D_WE(D_WE), .D_IN(D_DATA), .D_OUT(D_DATA));  // open: _0_ENA
  REGS16_32 REG0_9 (
    .A_ENA(A_8), .A_WE(A_WE), .A_IN(A_DATA), .A_OUT(A_DATA), .B_ENA(B_8), .B_WE(B_WE), .B_IN(B_DATA),
    .B_OUT(B_DATA), .C_ENA(C_8), .C_WE(C_WE), .C_IN(C_DATA), .C_OUT(C_DATA), .REG_A_ADDR(A_ADDR[3:0]),
    .REG_B_ADDR(B_ADDR[3:0]), .REG_C_ADDR(C_ADDR[3:0]), .CLK(CLK), .REG_D_ADDR(D_ADDR[3:0]), .D_ENA(D_8),
    .D_WE(D_WE), .D_IN(D_DATA), .D_OUT(D_DATA));  // open: _0_ENA
  REGS16_32 REG0_10 (
    .A_ENA(A_9), .A_WE(A_WE), .A_IN(A_DATA), .A_OUT(A_DATA), .B_ENA(B_9), .B_WE(B_WE), .B_IN(B_DATA),
    .B_OUT(B_DATA), .C_ENA(C_9), .C_WE(C_WE), .C_IN(C_DATA), .C_OUT(C_DATA), .REG_A_ADDR(A_ADDR[3:0]),
    .REG_B_ADDR(B_ADDR[3:0]), .REG_C_ADDR(C_ADDR[3:0]), .CLK(CLK), .REG_D_ADDR(D_ADDR[3:0]), .D_ENA(D_9),
    .D_WE(D_WE), .D_IN(D_DATA), .D_OUT(D_DATA));  // open: _0_ENA
  REGS16_32 REG0_11 (
    .A_ENA(A_A), .A_WE(A_WE), .A_IN(A_DATA), .A_OUT(A_DATA), .B_ENA(B_A), .B_WE(B_WE), .B_IN(B_DATA),
    .B_OUT(B_DATA), .C_ENA(C_A), .C_WE(C_WE), .C_IN(C_DATA), .C_OUT(C_DATA), .REG_A_ADDR(A_ADDR[3:0]),
    .REG_B_ADDR(B_ADDR[3:0]), .REG_C_ADDR(C_ADDR[3:0]), .CLK(CLK), .REG_D_ADDR(D_ADDR[3:0]), .D_ENA(D_A),
    .D_WE(D_WE), .D_IN(D_DATA), .D_OUT(D_DATA));  // open: _0_ENA
  REGS16_32 REG0_12 (
    .A_ENA(A_B), .A_WE(A_WE), .A_IN(A_DATA), .A_OUT(A_DATA), .B_ENA(B_B), .B_WE(B_WE), .B_IN(B_DATA),
    .B_OUT(B_DATA), .C_ENA(C_B), .C_WE(C_WE), .C_IN(C_DATA), .C_OUT(C_DATA), .REG_A_ADDR(A_ADDR[3:0]),
    .REG_B_ADDR(B_ADDR[3:0]), .REG_C_ADDR(C_ADDR[3:0]), .CLK(CLK), .REG_D_ADDR(D_ADDR[3:0]), .D_ENA(D_B),
    .D_WE(D_WE), .D_IN(D_DATA), .D_OUT(D_DATA));  // open: _0_ENA
  REGS16_32 REG0_13 (
    .A_ENA(A_C), .A_WE(A_WE), .A_IN(A_DATA), .A_OUT(A_DATA), .B_ENA(B_C), .B_WE(B_WE), .B_IN(B_DATA),
    .B_OUT(B_DATA), .C_ENA(C_C), .C_WE(C_WE), .C_IN(C_DATA), .C_OUT(C_DATA), .REG_A_ADDR(A_ADDR[3:0]),
    .REG_B_ADDR(B_ADDR[3:0]), .REG_C_ADDR(C_ADDR[3:0]), .CLK(CLK), .REG_D_ADDR(D_ADDR[3:0]), .D_ENA(D_C),
    .D_WE(D_WE), .D_IN(D_DATA), .D_OUT(D_DATA));  // open: _0_ENA
  REGS16_32 REG0_14 (
    .A_ENA(A_D), .A_WE(A_WE), .A_IN(A_DATA), .A_OUT(A_DATA), .B_ENA(B_D), .B_WE(B_WE), .B_IN(B_DATA),
    .B_OUT(B_DATA), .C_ENA(C_D), .C_WE(C_WE), .C_IN(C_DATA), .C_OUT(C_DATA), .REG_A_ADDR(A_ADDR[3:0]),
    .REG_B_ADDR(B_ADDR[3:0]), .REG_C_ADDR(C_ADDR[3:0]), .CLK(CLK), .REG_D_ADDR(D_ADDR[3:0]), .D_ENA(D_D),
    .D_WE(D_WE), .D_IN(D_DATA), .D_OUT(D_DATA));  // open: _0_ENA
  REGS16_32 REG0_15 (
    .A_ENA(A_E), .A_WE(A_WE), .A_IN(A_DATA), .A_OUT(A_DATA), .B_ENA(B_E), .B_WE(B_WE), .B_IN(B_DATA),
    .B_OUT(B_DATA), .C_ENA(C_E), .C_WE(C_WE), .C_IN(C_DATA), .C_OUT(C_DATA), .REG_A_ADDR(A_ADDR[3:0]),
    .REG_B_ADDR(B_ADDR[3:0]), .REG_C_ADDR(C_ADDR[3:0]), .CLK(CLK), .REG_D_ADDR(D_ADDR[3:0]), .D_ENA(D_E),
    .D_WE(D_WE), .D_IN(D_DATA), .D_OUT(D_DATA));  // open: _0_ENA
  REGS16_32 REG0_16 (
    .A_ENA(A_F), .A_WE(A_WE), .A_IN(A_DATA), .A_OUT(A_DATA), .B_ENA(B_F), .B_WE(B_WE), .B_IN(B_DATA),
    .B_OUT(B_DATA), .C_ENA(C_F), .C_WE(C_WE), .C_IN(C_DATA), .C_OUT(C_DATA), .REG_A_ADDR(A_ADDR[3:0]),
    .REG_B_ADDR(B_ADDR[3:0]), .REG_C_ADDR(C_ADDR[3:0]), .CLK(CLK), .REG_D_ADDR(D_ADDR[3:0]), .D_ENA(D_F),
    .D_WE(D_WE), .D_IN(D_DATA), .D_OUT(D_DATA));  // open: _0_ENA

  // Other names for the same wires on the sheet: A_ADR_LO[3:0] = A_ADDR[3:0]; A_ADR_HI[3:0] = A_ADDR[7:4];
  //   B_ADR_LO[3:0] = B_ADDR[3:0]; B_ADR_HI[3:0] = B_ADDR[7:4]; C_ADR_LO[3:0] = C_ADDR[3:0];
  //   C_ADR_HI[3:0] = C_ADDR[7:4]; D_ADR_LO[3:0] = D_ADDR[3:0]; D_ADR_HI[3:0] = D_ADDR[7:4]

  // Notes on the sheet:
  //   D_OUT: pull=down
  //   B_IN: pull=down
  //   D_IN: pull=down
  //   B_OUT: pull=down
  //   B_ADDR: pull=down
  //   B_WE: pull=down
  //   D_WE: pull=down
  //   A_OUT: pull=down
  //   C_OUT: pull=down
  //   C_WE: pull=down
  //   B_ENA: pull=down
  //   A_WE: pull=down
  //   A_ADDR: pull=down
  //   A_ENA: pull=down
  //   D_ADDR: pull=down
  //   C_ADDR: pull=down
  //   C_ENA: pull=down
  //   D_ENA: pull=down
  //   C_IN: pull=down
  //   A_IN: pull=down
endmodule

module INTERRUPT_STACK (
  input  CLK,
  input  [31:0] DATA_IN,
  input  POP,
  input  PUSH,
  input  ENA,
  output [31:0] DATA_OUT
);

  wire _1, _2, _3, _CLK, buffer_3_out, button_1_out, button_2_out, DEC, INC, not_2_out, or_2_out, WE;
  wire [0:0] decoder_1_out0;
  wire [7:0] counter_1_q;
  wire [31:0] pull_resistor_6_node;

  buf buffer_1 (DEC, _1);
  Pull_Resistor pull_resistor_1 (.node(_1));
  Pull_Resistor pull_resistor_2 (.node(_2));
  Pull_Resistor pull_resistor_3 (.node(_3));
  not not_1 (_CLK, CLK);
  or or_1 (WE, _2, buffer_3_out);
  buf buffer_2 (INC, _2);
  buf buffer_3 (buffer_3_out, _3);
  Decoder #(.select(2)) decoder_1 (
    .out0(decoder_1_out0[0]), .out1(_1), .out2(_2), .out3(_3), .sel({PUSH, POP}), .en(ENA));
  Pull_Resistor pull_resistor_4 (.node(DEC));
  or or_2 (or_2_out, DEC, INC);
  Pull_Resistor pull_resistor_5 (.node(or_2_out));
  Counter #(.ongoal("stay")) counter_1 (
    .load(DEC), .count(or_2_out), .Q(counter_1_q), .clk(CLK), .clr(button_1_out));  // open: D, carry
  Button button_1 (.out(button_1_out));
  Pull_Resistor pull_resistor_6 (.node(pull_resistor_6_node));
  assign pull_resistor_6_node = WE ? DATA_IN : 32'bz;  // Controlled_Buffer controlled_buffer_1
  Button button_2 (.out(button_2_out));
  not not_2 (not_2_out, WE);
  RAM #(.dataWidth(32), .bus("separate")) ram_1 (
    .addr(counter_1_q), .din(pull_resistor_6_node), .data(DATA_OUT), .str(WE), .sel(ENA), .clk(_CLK),
    .ld(not_2_out), .clr(button_2_out));

  // Notes on the sheet:
  //   CLK: pull=down
  //   ENA: pull=down
  //   DATA_IN: pull=down
  //   PUSH: pull=down
  //   DATA_OUT: pull=down
  //   POP: pull=down
endmodule
